# Fritzing sketch CanINO (saved by Fritzing 0.9.10b)
breadboards: 1

parts:
  Part1 = Arduino Uno (Rev3)
  U1 = POT [knob_status=50% power=0.5W package=pot_mammoth]
  Grove1 = Grove OLED 128x96
  J2 = Basic Servo  # not connected
  J3 = Basic Servo  # not connected
  ZS-042_RTC1 = ZS-042 RTC Module
  Part2 = HX711 Weighing Sensor Module
  S1 = Pushbutton [package="[SMD]"]
  U5 = SWITCH-SPST-2 [package=switch-spst-vertical]
  Load_Cell2 = Load Cell - Red/white/black/green
  Grove2 = Grove OLED 128x96  # not connected

nets:
  N1: Part1.A0, U1.A
  N2: Part1.A4/SDA, Grove1.SCL, ZS-042_RTC1.SDA
  N3: Part1.A5/SCL, Grove1.SDA, ZS-042_RTC1.SCL
  N4: Part1.D2, U5.P
  N5: Part1.D3_PWM, S1.Pin_3, S1.Pin_4
  N6: Part1.D6_PWM, Part2.DO/RX
  N7: Part1.D7, Part2.CK/TX
  VCC: Part1.5V, U1.S, Grove1.VCC, ZS-042_RTC1.VCC, Part2.VCC, S1.Pin_1, S1.Pin_2
  GND: Part1.GND, U1.E, Grove1.GND, ZS-042_RTC1.GND, Part2.GND, U5.O
  N8: Part2.E+, Load_Cell2.wire1
  N9: Part2.E-, Load_Cell2.wire3
  N10: Part2.A+, Load_Cell2.wire4
  N11: Part2.A-, Load_Cell2.wire2

notes:
  SetupMode

custom parts:
  Load Cell - Red/white/black/green: A rectangle load cell/weighting pressure Sensor with four wires - Red, white, black, green. Normally corresponding with E+, E-, A+, A- respectively.
